# Fritzing sketch MegaW5100 (saved by Fritzing 0.9.3b)
breadboards: 1

parts:
  Componente2 = Arduino Mega 2560 (Rev3)
  Componente4 = Arduino Ethernet Shield (Rev3)
  R1 = Resistor [tolerance=±5% resistance=330 package=THT]
  R2 = Resistor [tolerance=±5% resistance=10k package=THT]
  R3 = Resistor [tolerance=±5% resistance=330 package=THT]
  R4 = Resistor [tolerance=±5% resistance=10k package=THT]
  R5 = Resistor [tolerance=±5% resistance=330 package=THT]
  R6 = Resistor [tolerance=±5% resistance=10k package=THT]
  U1 = LIPO-2000mAh [package=lipo-2000]
  U2 = LIPO-2000mAh [package=lipo-2000]
  U3 = LIPO-2000mAh [package=lipo-2000]
  D1 = SOLAR-IXYS [package=solarbit-12x1]
  U4 = ACS712 [package=so08]  # not connected
  U5 = ACS712 [package=so08]  # not connected
  U6 = ACS712 [package=so08]  # not connected

nets:
  GND: Componente2.GND, Componente4.GND, R2.Pin_1, R4.Pin_1, R6.Pin_1
  N1: Componente2.D11_PWM, Componente4.ETH_CS
  N2: Componente2.RESET, Componente4.RESET
  N3: Componente2.3V3, U2.-, D1.A
  5V: Componente2.5V, Componente4.5V
  N4: Componente2.D4_PWM, Componente4.SDCS
  N5: Componente2.D50, Componente4.ICSP_MISO
  N6: Componente2.D51, Componente4.ICSP_MOSI
  N7: Componente2.D52, Componente4.ICSP_SCK
  N8: R1.Pin_0, U3.+
  N9: R1.Pin_1, R2.Pin_0
  N10: R3.Pin_0, D1.C
  N11: R3.Pin_1, R4.Pin_0
  N12: R5.Pin_1, R6.Pin_0
  N13: U1.+, U3.-
  N14: U1.-, U2.+
